// Logisim project alu.circ as structural Verilog: 7 circuits, main circuit main
module main (
  input  [31:0] X,
  input  [31:0] Y,
  input  [5:0] Switch__S,
  output Signed_Overflow,
  output [31:0] RESULT,
  output Equal
);

  wire bitpal_1_out, comparator_2_lt, comparator_3_lt;
  wire [4:0] bit_extender_1_out;
  wire [31:0] adder_1_out, adder_2_out, and_1_out, bit_extender_2_out, bit_extender_3_out,
       bit_extender_4_out, lfsr_1_out, or_1_out, shifter_1_out, shifter_2_out, shifter_3_out,
       subtractor_1_out, subtractor_2_out;

  Bit_Extender #(.in_width(32), .out_width(5)) bit_extender_1 (.in(Y), .out(bit_extender_1_out));
  Comparator #(.width(32)) comparator_1 (.a(Y), .b(X), .eq(Equal));  // open: gt, lt
  Shifter #(.width(32)) shifter_1 (.in(X), .\dist (bit_extender_1_out), .out(shifter_1_out));
  Shifter #(.width(32), .shift("lr")) shifter_2 (.in(X), .\dist (bit_extender_1_out), .out(shifter_2_out));
  Shifter #(.width(32), .shift("ar")) shifter_3 (.in(X), .\dist (bit_extender_1_out), .out(shifter_3_out));
  Adder #(.width(32)) adder_1 (.a(X), .b(Y), .out(adder_1_out));  // open: cin, cout
  Adder #(.width(32)) adder_2 (.a(X), .b(Y), .out(adder_2_out));  // open: cin, cout
  Subtractor #(.width(32)) subtractor_1 (.a(X), .b(Y), .out(subtractor_1_out));  // open: bin, bout
  Subtractor #(.width(32)) subtractor_2 (.a(X), .b(Y), .out(subtractor_2_out));  // open: bin, bout
  assign and_1_out = X & Y;  // AND_Gate and_1, 32 bits wide
  assign or_1_out = X | Y;  // OR_Gate or_1, 32 bits wide
  Comparator #(.width(32)) comparator_2 (.a(X), .b(Y), .lt(comparator_2_lt));  // open: gt, eq
  Comparator #(.width(32), .mode("unsigned")) comparator_3 (.a(X), .b(Y), .lt(comparator_3_lt));  // open: gt, eq
  bitpal bitpal_1 (.in_1(X), .out(bitpal_1_out));
  lfsr lfsr_1 (.\input (X), .out(lfsr_1_out));
  checkoverflow checkoverflow_1 (
    .Y(Y), .X(X), .switch(Switch__S), .difference(subtractor_1_out), .sum(adder_1_out), .out(Signed_Overflow));
  assign bit_extender_2_out = {{31{1'b0}}, comparator_2_lt};  // Bit_Extender bit_extender_2
  assign bit_extender_3_out = {{31{1'b0}}, comparator_3_lt};  // Bit_Extender bit_extender_3
  assign bit_extender_4_out = {{31{1'b0}}, bitpal_1_out};  // Bit_Extender bit_extender_4
  Multiplexer #(.select(5), .width(32), .enable("false")) multiplexer_1 (
    .in0(shifter_1_out), .in2(shifter_2_out), .in3(shifter_3_out), .in16(adder_1_out), .in17(adder_2_out),
    .in18(subtractor_1_out), .in19(subtractor_2_out), .in20(and_1_out), .in21(or_1_out),
    .in26(bit_extender_2_out), .in27(bit_extender_3_out), .in30(bit_extender_4_out), .in31(lfsr_1_out),
    .out(RESULT), .sel({Switch__S[5], Switch__S[3:0]}));  // open: in1, in4, in5, in6, in7, in8, in9, in10, in11, in12, in13, in14, in15, in22, in23, in24, in25, in28, in29

  // Notes on the sheet:
  //   INPUTS to your circuit
  //   INPUT to your circuit
  //   DON'T CHANGE THE INPUTS AND OUTPUTS! IF YOU DO SO, YOU NEED TO MAKE SURE THE PINS ARE IN THE RIGHT PLACES!
  //   OUTPUTS of your circuit
endmodule

module bitpal (
  input  [31:0] in_1,
  output out
);

  Comparator #(.width(16)) comparator_1 (
    .a({in_1[0], in_1[1], in_1[2], in_1[3], in_1[4], in_1[5], in_1[6], in_1[7], in_1[8], in_1[9], in_1[10], in_1[11], in_1[12], in_1[13], in_1[14], in_1[15]}),
    .b(in_1[31:16]), .eq(out));  // open: gt, lt
endmodule

module lfsr (
  input  [31:0] \input ,
  output [31:0] out
);

  wire xor_2_out, xor_3_out;

  xor xor_1 (out[15], xor_2_out, \input [5]);
  xor xor_2 (xor_2_out, xor_3_out, \input [3]);
  xor xor_3 (xor_3_out, \input [0], \input [2]);

  assign {out[31:16], out[14:0]} = \input [31:1];
endmodule

module checkoverflow (
  input  [31:0] Y,
  input  [31:0] difference,
  input  [31:0] sum,
  input  [31:0] X,
  input  [5:0] switch,
  output out
);

  wire comparator_1_eq, comparator_2_eq, comparator_3_eq, comparator_3_lt, even_parity_1_out,
       multiplexer_1_out, multiplexer_2_out, negativeoverflow_1_out, postive_overflow_1_out;

  negativeoverflow negativeoverflow_1 (.Y(Y), .X(X), .difference(difference), .out(negativeoverflow_1_out));
  Comparator #(.width(6)) comparator_1 (.a(6'b100000), .b(switch), .eq(comparator_1_eq));  // open: gt, lt
  Comparator #(.width(6)) comparator_2 (.a(6'b100010), .b(switch), .eq(comparator_2_eq));  // open: gt, lt
  Comparator #(.width(6)) comparator_3 (
    .a(switch), .b(6'b100000), .eq(comparator_3_eq), .lt(comparator_3_lt));  // open: gt
  xnor even_parity_1 (even_parity_1_out, comparator_3_eq, comparator_3_lt);
  postive_overflow postive_overflow_1 (.Y(Y), .X(X), .sum(sum), .out(postive_overflow_1_out));
  Multiplexer #(.enable("false")) multiplexer_1 (
    .in0(1'b0), .in1(postive_overflow_1_out), .out(multiplexer_1_out), .sel(comparator_1_eq));
  Multiplexer #(.enable("false")) multiplexer_2 (
    .in0(1'b0), .in1(negativeoverflow_1_out), .out(multiplexer_2_out), .sel(comparator_2_eq));
  Multiplexer #(.enable("false")) multiplexer_3 (
    .in0(multiplexer_1_out), .in1(multiplexer_2_out), .out(out), .sel(even_parity_1_out));
endmodule

module signcheck (
  input  [31:0] input1,
  input  [31:0] input2,
  output out
);

  wire comparator_1_lt, comparator_2_lt;

  Comparator #(.width(32)) comparator_1 (.a(input1), .b({32{1'b0}}), .lt(comparator_1_lt));  // open: gt, eq
  Comparator #(.width(32)) comparator_2 (.a(input2), .b({32{1'b0}}), .lt(comparator_2_lt));  // open: gt, eq
  xor xor_1 (out, comparator_1_lt, comparator_2_lt);
endmodule

module negativeoverflow (
  input  [31:0] difference,
  input  [31:0] Y,
  input  [31:0] X,
  output out
);

  wire not_1_out, signcheck_1_out, signcheck_2_out;

  signcheck signcheck_1 (.input1(difference), .input2(Y), .out(signcheck_1_out));
  not not_1 (not_1_out, signcheck_1_out);
  signcheck signcheck_2 (.input1(Y), .input2(X), .out(signcheck_2_out));
  and and_1 (out, not_1_out, signcheck_2_out);
endmodule

module postive_overflow (
  input  [31:0] sum,
  input  [31:0] Y,
  input  [31:0] X,
  output out
);

  wire not_1_out, signcheck_1_out, signcheck_2_out;

  signcheck signcheck_1 (.input1(sum), .input2(Y), .out(signcheck_1_out));
  signcheck signcheck_2 (.input1(Y), .input2(X), .out(signcheck_2_out));
  not not_1 (not_1_out, signcheck_2_out);
  and and_1 (out, signcheck_1_out, not_1_out);
endmodule
