// Logisim project cpu.circ as structural Verilog: 3 circuits, main circuit main
// LBU_OUT
module main (
  input  [31:0] RS_READ_VALUE,
  input  [31:0] RT_READ_VALUE,
  input  [31:0] INSTRUCTION,
  input  CLOCK,
  input  RESET,
  output [31:0] t0,
  output [31:0] t1,
  output [31:0] t2,
  output [31:0] t3,
  output [4:0] RS,
  output [4:0] RT,
  output [4:0] Write_Register,
  output [31:0] RD_WRITE_VALUE,
  output RD_WRITE_ENABLE,
  output [23:0] FETCH_ADDRESS
);

  wire AccessByte, ALU_signed_overflow, AluOp, Alusrc, bne, branch, Branch_Taken, Equal, ExtOp, jal, jr,
       jumps, Kill_Inst, lb, Lui, Memread, MemtoReg, Memwrite, multiplexer_2_out, multiplexer_3_out,
       not_1_out, reg_select_3_is__tx, RegDest, Shift, temp_rs, temp_rt;
  wire [1:0] rs_to_regfile, rt_to_regfile;
  wire [4:0] multiplexer_14_out;
  wire [4:2] demultiplexer_1_out1, demultiplexer_2_out1;
  wire [5:0] AluCtrl, multiplexer_13_out, OP;
  wire [7:0] bit_extender_4_out;
  wire [23:0] adder_1_out, adder_2_out, adder_3_out, multiplexer_6_out, multiplexer_7_out, NEW_PC,
       subtractor_1_out, subtractor_2_out;
  wire [25:0] ADDR;
  wire [31:0] adder_4_out, ALU_RESULT, bit_extender_1_out, bit_extender_2_out, bit_extender_3_out,
       bit_extender_6_out, EXT_ADDR_IMM, LB_OUT, MEM_data_mem_out, MEM_RESULT, multiplexer_1_out,
       multiplexer_8_out, multiplexer_10_out, multiplexer_11_out, multiplexer_16_out, multiplexer_18_out,
       RS_READ, RS_READ_OUT, RT_READ, RT_READ_OUT, shifter_1_out;

  Register #(.width(24)) register_1 (.D(NEW_PC), .Q(FETCH_ADDRESS), .clk(CLOCK));  // open: en, clr
  Multiplexer #(.width(32), .enable("false")) multiplexer_1 (
    .in0(INSTRUCTION), .in1({32{1'b0}}), .out(multiplexer_1_out), .sel(Kill_Inst));
  reg_select reg_select_1 (.Register(ADDR[20:16]), .Is__tx(temp_rt));
  Demultiplexer #(.width(5), .enable("false")) demultiplexer_1 (
    .out0(RT), .out1({demultiplexer_1_out1, rt_to_regfile}), .in(ADDR[20:16]), .sel(temp_rt));
  Register #(.width(32)) register_2 (.D(multiplexer_1_out), .Q({OP, ADDR}), .clk(CLOCK));  // open: en, clr
  Demultiplexer #(.width(5), .enable("false")) demultiplexer_2 (
    .out0(RS), .out1({demultiplexer_2_out1, rs_to_regfile}), .in(ADDR[25:21]), .sel(temp_rs));
  reg_select reg_select_2 (.Register(ADDR[25:21]), .Is__tx(temp_rs));
  or or_1 (Kill_Inst, Branch_Taken, jr, jumps);
  Adder #(.width(24)) adder_1 (.a(FETCH_ADDRESS), .b(24'h1), .out(adder_1_out));  // open: cin, cout
  Multiplexer #(.enable("false")) multiplexer_2 (
    .in0(1'b0), .in1(RD_WRITE_ENABLE), .out(multiplexer_2_out), .sel(reg_select_3_is__tx));
  reg_select reg_select_3 (.Register(Write_Register), .Is__tx(reg_select_3_is__tx));
  Adder #(.width(24)) adder_2 (.a(FETCH_ADDRESS), .b(EXT_ADDR_IMM[23:0]), .out(adder_2_out));  // open: cin, cout
  and and_1 (Branch_Taken, branch, multiplexer_3_out);
  Multiplexer #(.enable("false")) multiplexer_3 (.in0(Equal), .in1(not_1_out), .out(multiplexer_3_out), .sel(bne));
  Multiplexer #(.width(32), .enable("false")) multiplexer_4 (
    .in0(RS_READ_VALUE), .in1(RS_READ_OUT), .out(RS_READ), .sel(temp_rs));
  Multiplexer #(.width(32), .enable("false")) multiplexer_5 (
    .in0(RT_READ_VALUE), .in1(RT_READ_OUT), .out(RT_READ), .sel(temp_rt));
  regfile_main RegFile (
    .write_register(Write_Register[1:0]), .write_data(RD_WRITE_VALUE), .Read_Data_1(RS_READ_OUT),
    .Read_Data_2(RT_READ_OUT), .t0_Value(t0), .t1_Value(t1), .t2_Value(t2), .t3_Value(t3),
    .Read_register_1(rs_to_regfile), .Read_register_2(rt_to_regfile), .RegWrite(multiplexer_2_out),
    .clock(CLOCK));
  Multiplexer #(.width(24), .enable("false")) multiplexer_6 (
    .in0(adder_1_out), .in1(adder_2_out), .out(multiplexer_6_out), .sel(Branch_Taken));
  not not_1 (not_1_out, Equal);
  control control_1 (
    .opcode(OP), .funct(ADDR[5:0]), .RegDst(RegDest), .ALUSrc(Alusrc), .Mem2Reg(MemtoReg), .Shift(Shift),
    .MemRead(Memread), .MemWrite(Memwrite), .ALUCtrl(AluCtrl), .Branch(branch), .ExtOp(ExtOp),
    .AccessByte(AccessByte), .lui(Lui), .lb(lb), .AluOp(AluOp), .bne(bne), .jumps(jumps), .jr(jr), .jal(jal),
    .RD_WRITE_ENABLE(RD_WRITE_ENABLE));
  Subtractor #(.width(24)) subtractor_1 (.a(RS_READ[23:0]), .b(24'h100000), .out(subtractor_1_out));  // open: bin, bout
  assign bit_extender_1_out = {{16{ADDR[15]}}, ADDR[15:0]};  // Bit_Extender bit_extender_1
  assign bit_extender_2_out = {{16{1'b0}}, ADDR[15:0]};  // Bit_Extender bit_extender_2
  Multiplexer #(.width(24), .enable("false")) multiplexer_7 (
    .in0(multiplexer_6_out), .in1(subtractor_1_out), .out(multiplexer_7_out), .sel(jr));
  Multiplexer #(.width(32), .enable("false")) multiplexer_8 (
    .in0(RT_READ), .in1(EXT_ADDR_IMM), .out(multiplexer_8_out), .sel(Alusrc));
  assign bit_extender_3_out = {{27{1'b0}}, ADDR[10:6]};  // Bit_Extender bit_extender_3
  Multiplexer #(.width(32), .enable("false")) multiplexer_9 (
    .in0(bit_extender_1_out), .in1(bit_extender_2_out), .out(EXT_ADDR_IMM), .sel(ExtOp));
  Subtractor #(.width(24)) subtractor_2 (.a(ADDR[23:0]), .b(24'h100000), .out(subtractor_2_out));  // open: bin, bout
  Multiplexer #(.width(32), .enable("false")) multiplexer_10 (
    .in0(RS_READ), .in1(RT_READ), .out(multiplexer_10_out), .sel(Shift));
  Multiplexer #(.width(32), .enable("false")) multiplexer_11 (
    .in0(multiplexer_8_out), .in1(bit_extender_3_out), .out(multiplexer_11_out), .sel(Shift));
  Multiplexer #(.width(24), .enable("false")) multiplexer_12 (
    .in0(multiplexer_7_out), .in1(subtractor_2_out), .out(NEW_PC), .sel(jumps));
  alu_main ALU (
    .Switch__S(multiplexer_13_out), .X(multiplexer_10_out), .Equal(Equal), .RESULT(ALU_RESULT),
    .Signed_Overflow(ALU_signed_overflow), .Y(multiplexer_11_out));
  Multiplexer #(.width(6), .enable("false")) multiplexer_13 (
    .in0(AluCtrl), .in1(6'b100001), .out(multiplexer_13_out), .sel(AluOp));
  LED led_1 (.in(ALU_signed_overflow));
  Multiplexer #(.width(5), .enable("false")) multiplexer_14 (
    .in0(ADDR[20:16]), .in1(ADDR[15:11]), .out(multiplexer_14_out), .sel(RegDest));
  mem_main MEM (
    .Data_Mem_Addr(ALU_RESULT), .Data_Mem_In(RT_READ), .ACCESS_BYTE(AccessByte), .MEM_WRITE(Memwrite),
    .CLOCK(CLOCK), .Data_Mem_Out(MEM_data_mem_out));
  Bit_Extender #(.in_width(32), .out_width(8)) bit_extender_4 (.in(MEM_data_mem_out), .out(bit_extender_4_out));
  Multiplexer #(.width(32), .enable("false")) multiplexer_15 (
    .in0(MEM_data_mem_out), .in1(LB_OUT), .out(MEM_RESULT), .sel(lb));
  Multiplexer #(.width(32), .enable("false")) multiplexer_16 (
    .in0(ALU_RESULT), .in1(MEM_RESULT), .out(multiplexer_16_out), .sel(MemtoReg));
  Shifter #(.width(32)) shifter_1 (.in(EXT_ADDR_IMM), .\dist (5'b10000), .out(shifter_1_out));
  Adder #(.width(24)) adder_3 (.a(FETCH_ADDRESS), .b(24'h100000), .out(adder_3_out));  // open: cin, cout
  Multiplexer #(.width(5), .enable("false")) multiplexer_17 (
    .in0(multiplexer_14_out), .in1({5{1'b1}}), .out(Write_Register), .sel(jal));
  assign LB_OUT = {{24{bit_extender_4_out[7]}}, bit_extender_4_out};  // Bit_Extender bit_extender_5
  Multiplexer #(.width(32), .enable("false")) multiplexer_18 (
    .in0(multiplexer_16_out), .in1(shifter_1_out), .out(multiplexer_18_out), .sel(Lui));
  assign bit_extender_6_out = {{8{adder_3_out[23]}}, adder_3_out};  // Bit_Extender bit_extender_6
  Adder #(.width(32)) adder_4 (.a(bit_extender_6_out), .b({32{1'b0}}), .out(adder_4_out));  // open: cin, cout
  Multiplexer #(.width(32), .enable("false")) multiplexer_19 (
    .in0(multiplexer_18_out), .in1(adder_4_out), .out(RD_WRITE_VALUE), .sel(jal));

  // Other names for the same wires on the sheet: ADDR_IMM[15:0] = ADDR[15:0]; FUNCT[5:0] = ADDR[5:0];
  //   SHAMT[4:0] = ADDR[10:6]; RD[4:0] = ADDR[15:11]; RT_t[4:0] = ADDR[20:16]; RS_t[4:0] = ADDR[25:21];
  //   PC[23:0] = FETCH_ADDRESS; rs_to_run[4:0] = RS; rt_to_run[4:0] = RT

  // Notes on the sheet:
  //   These are outputs/inputs from run.circ
  //   Kill Instruction Logic
  //   Choosing Regfile/Run Input
  //   Instruction Decode Logic
  //   These are outputs to run.circ
  //   Sign/Zero Extend Logic
  //   Choosing Regfile/Run output
  //   Regfile logic
  //   Branch, Jump, PC logic
  //   Immediate Sign Extension
  //   Control Logic
  //   ALU
  //   Write Register Logic
  //   Memory Logic
  //   RD_Write_Value source
  //   Lui Logic
endmodule

module reg_select (
  input  [4:0] Register,
  output Is__tx
);

  wire comparator_1_lt, comparator_2_gt;

  Comparator #(.width(5)) comparator_1 (.a(Register), .b(5'b01100), .lt(comparator_1_lt));  // open: gt, eq
  Comparator #(.width(5)) comparator_2 (.a(Register), .b(5'b00111), .gt(comparator_2_gt));  // open: eq, lt
  and and_1 (Is__tx, comparator_2_gt, comparator_1_lt);
endmodule

module control (
  input  [5:0] opcode,
  input  [5:0] funct,
  output RegDst,
  output ALUSrc,
  output Mem2Reg,
  output Shift,
  output MemRead,
  output MemWrite,
  output [5:0] ALUCtrl,
  output Branch,
  output ExtOp,
  output AccessByte,
  output lui,
  output lb,
  output AluOp,
  output bne,
  output jumps,
  output jr,
  output jal,
  output RD_WRITE_ENABLE
);

  wire addiu, and_4_out, and_5_out, and_9_out, andi, comparator_1_eq, comparator_2_eq, comparator_3_eq, j,
       not_1_out, not_2_out, not_3_out, not_4_out, not_5_out, not_6_out, not_7_out, not_8_out, not_9_out,
       not_10_out, not_11_out, not_12_out, not_13_out, not_14_out, not_15_out, not_16_out, not_17_out,
       not_18_out, not_19_out, not_20_out, not_21_out, not_22_out, not_23_out, not_24_out, not_25_out,
       not_26_out, not_27_out, not_28_out, not_29_out, not_30_out, not_31_out, not_32_out, not_33_out,
       not_34_out, not_35_out, not_36_out, not_37_out, not_38_out, not_39_out, not_40_out, not_41_out,
       not_42_out, not_43_out, not_44_out, not_45_out, not_46_out, not_47_out, not_48_out, not_49_out,
       not_50_out, not_51_out, not_52_out, not_53_out, not_54_out, not_55_out, not_56_out, not_57_out,
       not_58_out, not_59_out, or_2_out, ori;
  wire [1:0] multiplexer_2_out;

  not not_1 (not_1_out, Branch);
  not not_2 (not_2_out, jumps);
  not not_3 (not_3_out, RegDst);
  not not_4 (not_4_out, opcode[2]);
  not not_5 (not_5_out, opcode[1]);
  not not_6 (not_6_out, opcode[4]);
  not not_7 (not_7_out, opcode[3]);
  not not_8 (not_8_out, opcode[5]);
  not not_9 (not_9_out, opcode[0]);
  and and_1 (RegDst, not_8_out, not_6_out, not_7_out, not_4_out, not_5_out, not_9_out);
  Multiplexer #(.select(2), .width(6), .enable("false")) multiplexer_1 (
    .in0(funct), .in1(6'b100001), .in2(6'b100100), .in3(6'b100101), .out(ALUCtrl), .sel(multiplexer_2_out));
  not not_10 (not_10_out, opcode[2]);
  not not_11 (not_11_out, opcode[5]);
  not not_12 (not_12_out, opcode[1]);
  not not_13 (not_13_out, opcode[4]);
  and and_2 (addiu, not_11_out, not_13_out, opcode[3], not_10_out, not_12_out, opcode[0]);
  and and_3 (ALUSrc, not_1_out, not_2_out, not_3_out);
  Multiplexer #(.width(2), .enable("false")) multiplexer_2 (
    .in1(2'b11), .out(multiplexer_2_out), .sel(ori));  // open: in0
  Multiplexer #(.width(2), .enable("false")) multiplexer_3 (
    .in1(2'b10), .out(multiplexer_2_out), .sel(andi));  // open: in0
  not not_14 (not_14_out, opcode[2]);
  not not_15 (not_15_out, opcode[4]);
  not not_16 (not_16_out, opcode[3]);
  and and_4 (and_4_out, opcode[5], not_15_out, not_16_out, not_14_out, opcode[1], opcode[0]);
  Multiplexer #(.width(2), .enable("false")) multiplexer_4 (
    .in1(2'b00), .out(multiplexer_2_out), .sel(RegDst));  // open: in0
  Multiplexer #(.width(2), .enable("false")) multiplexer_5 (
    .in1(2'b01), .out(multiplexer_2_out), .sel(addiu));  // open: in0
  not not_17 (not_17_out, opcode[4]);
  not not_18 (not_18_out, opcode[1]);
  not not_19 (not_19_out, opcode[0]);
  not not_20 (not_20_out, opcode[3]);
  and and_5 (and_5_out, opcode[5], not_17_out, not_20_out, opcode[2], not_18_out, not_19_out);
  not not_21 (not_21_out, opcode[1]);
  not not_22 (not_22_out, opcode[4]);
  not not_23 (not_23_out, opcode[2]);
  not not_24 (not_24_out, opcode[0]);
  not not_25 (not_25_out, opcode[3]);
  and and_6 (lb, opcode[5], not_22_out, not_25_out, not_23_out, not_21_out, not_24_out);
  not not_26 (not_26_out, opcode[4]);
  not not_27 (not_27_out, opcode[5]);
  and and_7 (lui, not_27_out, not_26_out, opcode[3], opcode[2], opcode[1], opcode[0]);
  not not_28 (not_28_out, opcode[2]);
  not not_29 (not_29_out, opcode[4]);
  and and_8 (MemWrite, opcode[5], not_29_out, opcode[3], not_28_out, opcode[1], opcode[0]);
  Comparator #(.width(6)) comparator_1 (.a(funct), .b({6{1'b0}}), .eq(comparator_1_eq));  // open: gt, lt
  Comparator #(.width(6)) comparator_2 (.a(funct), .b(6'b000010), .eq(comparator_2_eq));  // open: gt, lt
  Comparator #(.width(6)) comparator_3 (.a(funct), .b(6'b000011), .eq(comparator_3_eq));  // open: gt, lt
  not not_30 (not_30_out, opcode[0]);
  not not_31 (not_31_out, opcode[1]);
  not not_32 (not_32_out, opcode[3]);
  not not_33 (not_33_out, opcode[4]);
  not not_34 (not_34_out, opcode[5]);
  and and_9 (and_9_out, not_34_out, not_33_out, not_32_out, opcode[2], not_31_out, not_30_out);
  or or_1 (AluOp, Mem2Reg, MemWrite);
  or or_2 (or_2_out, comparator_1_eq, comparator_2_eq, comparator_3_eq);
  not not_35 (not_35_out, opcode[5]);
  not not_36 (not_36_out, opcode[1]);
  not not_37 (not_37_out, opcode[4]);
  not not_38 (not_38_out, opcode[3]);
  and and_10 (bne, not_35_out, not_37_out, not_38_out, opcode[2], not_36_out, opcode[0]);
  and and_11 (Shift, RegDst, or_2_out);
  not not_39 (not_39_out, opcode[1]);
  not not_40 (not_40_out, opcode[5]);
  not not_41 (not_41_out, opcode[0]);
  not not_42 (not_42_out, opcode[4]);
  and and_12 (andi, not_40_out, not_42_out, opcode[3], opcode[2], not_39_out, not_41_out);
  not not_43 (not_43_out, opcode[1]);
  not not_44 (not_44_out, opcode[4]);
  not not_45 (not_45_out, opcode[5]);
  and and_13 (ori, not_45_out, not_44_out, opcode[3], opcode[2], not_43_out, opcode[0]);
  not not_46 (not_46_out, funct[1]);
  not not_47 (not_47_out, funct[4]);
  not not_48 (not_48_out, funct[5]);
  not not_49 (not_49_out, funct[2]);
  not not_50 (not_50_out, funct[0]);
  and and_14 (jr, not_48_out, not_47_out, funct[3], not_49_out, not_46_out, not_50_out);
  not not_51 (not_51_out, j);
  not not_52 (not_52_out, Branch);
  not not_53 (not_53_out, MemWrite);
  not not_54 (not_54_out, jr);
  not not_55 (not_55_out, opcode[2]);
  not not_56 (not_56_out, opcode[5]);
  not not_57 (not_57_out, opcode[3]);
  not not_58 (not_58_out, opcode[4]);
  and and_15 (jumps, not_56_out, not_58_out, not_57_out, not_55_out, opcode[1]);
  not not_59 (not_59_out, opcode[0]);
  or or_3 (Mem2Reg, and_4_out, and_5_out, lb);
  or or_4 (AccessByte, and_5_out, lb);
  or or_5 (Branch, bne, and_9_out);
  or or_6 (ExtOp, andi, ori);
  and and_16 (RD_WRITE_ENABLE, not_51_out, not_52_out, not_53_out, not_54_out);
  and and_17 (jal, opcode[0], jumps);
  and and_18 (j, jumps, not_59_out);

  assign MemRead = Mem2Reg;

  // Other names for the same wires on the sheet: Access_Byte = AccessByte; Branches = Branch; Logical_extend = ExtOp;
  //   Mem_Access = Mem2Reg; R_format = RegDst; sw = MemWrite

  // Notes on the sheet:
  //   addiu
  //   andi
  //   ori
  //   R-format
  //   ALU Src
  //   Alu Control
  //   addiu
  //   lw
  //   lbu
  //   lb
  //   lui
  //   sw
  //   Alu Op
  //   beq
  //   bne
  //   andi
  //   ori
  //   jr
  //   jump
  //   Write Enable
endmodule
