// Logisim project mem.circ as structural Verilog: 3 circuits, main circuit main
module main (
  input  [31:0] Data_Mem_Addr,
  input  [31:0] Data_Mem_In,
  input  ACCESS_BYTE,
  input  MEM_WRITE,
  input  CLOCK,
  output [31:0] Data_Mem_Out
);

  wire not_1_out;
  wire [1:0] extend_addr_1_byte_address;
  wire [23:0] extend_addr_1__24_bit_output;
  wire [31:0] Byte_Data_Out, ram_1_data, Word_Data_Out;

  extend_addr extend_addr_1 (
    ._32_bit_address_input(Data_Mem_Addr), ._24_bit_output(extend_addr_1__24_bit_output),
    .byte_address(extend_addr_1_byte_address));
  select_byte select_byte_1 (
    .byte_address(extend_addr_1_byte_address), .\input (Word_Data_Out), .byte_value(Byte_Data_Out));
  not not_1 (not_1_out, MEM_WRITE);
  RAM #(.addrWidth(24), .dataWidth(32), .bus("separate")) ram_1 (
    .addr(extend_addr_1__24_bit_output), .din(Data_Mem_In), .data(ram_1_data), .str(MEM_WRITE), .clk(CLOCK),
    .ld(not_1_out), .clr(1'b0));  // open: sel
  Multiplexer #(.width(32), .enable("false")) multiplexer_1 (
    .in0(ram_1_data), .out(Word_Data_Out), .sel(MEM_WRITE));  // open: in1
  Multiplexer #(.width(32), .enable("false")) multiplexer_2 (
    .in0(Word_Data_Out), .in1(Byte_Data_Out), .out(Data_Mem_Out), .sel(ACCESS_BYTE));

  // Other names for the same wires on the sheet: CLK = CLOCK

  // Notes on the sheet:
  //   These are INPUTS to the circuit
  //   These are INPUTS to the circuit
  //   DO NOT CHANGE THE LOCATIONS OF THE INPUTS/OUTPUTS! IF YOU DO SO, YOU NEED TO MAKE SURE THE PINS ARE AT THE RIGHT PLACE!
  //   Yet again, the clock is not an actual clock, but an input, one that will be driven from a higher circuit
  //   This is an OUTPUT to the circuit
endmodule

module extend_addr (
  input  [31:0] _32_bit_address_input,
  output [1:0] byte_address,
  output [23:0] _24_bit_output
);

  wire [31:26] subtractor_1_out;

  Subtractor #(.width(32)) subtractor_1 (
    .a(_32_bit_address_input), .b(32'h10010000), .out({subtractor_1_out, _24_bit_output, byte_address}));  // open: bin, bout
endmodule

module select_byte (
  input  [1:0] byte_address,
  input  [31:0] \input ,
  output [31:0] byte_value
);

  wire [7:0] multiplexer_1_out;

  Multiplexer #(.select(2), .width(8), .enable("false")) multiplexer_1 (
    .in0(\input [31:24]), .in1(\input [23:16]), .in2(\input [15:8]), .in3(\input [7:0]),
    .out(multiplexer_1_out), .sel(byte_address));
  assign byte_value = {{24{1'b0}}, multiplexer_1_out};  // Bit_Extender bit_extender_1
endmodule
