// Logisim project reg-insert.circ as structural Verilog: 1 circuit, main circuit main
module main (
  output [7:0] test_num,
  output [31:0] Reg_0_Value,
  output [31:0] Reg_1_Value,
  output [31:0] Reg_2_Value,
  output [31:0] Reg_3_Value,
  output halt,
  output [31:0] Read_Data_1,
  output [31:0] Read_Data_2
);

  wire clock_1_out;
  wire [6:0] rom_2_data;
  wire [7:0] adder_1_out;
  wire [31:0] WriteData;

  Register register_1 (.D(adder_1_out), .en(1'b1), .Q(test_num), .clk(clock_1_out));  // open: clr
  Adder adder_1 (.a(8'h1), .b(test_num), .out(adder_1_out));  // open: cin, cout
  Comparator comparator_1 (.a(test_num), .b(8'h4), .eq(halt));  // open: gt, lt
  ROM #(.dataWidth(32)) rom_1 (.addr(test_num), .data(WriteData));  // open: sel
  // Probe on rom_2_data
  ROM #(.dataWidth(7)) rom_2 (.addr(test_num), .data(rom_2_data), .sel(1'b1));
  Clock clock_1 (.out(clock_1_out));
  regfile_main main_1 (
    .write_register(rom_2_data[5:4]), .write_data(WriteData), .Read_Data_1(Read_Data_1),
    .Read_Data_2(Read_Data_2), .t0_Value(Reg_0_Value), .t1_Value(Reg_1_Value), .t2_Value(Reg_2_Value),
    .t3_Value(Reg_3_Value), .Read_register_1(rom_2_data[1:0]), .Read_register_2(rom_2_data[3:2]),
    .RegWrite(rom_2_data[6]), .clock(clock_1_out));

  // Notes on the sheet:
  //   contents of rom_1 (hex, n*v repeats v):
  //   beefbeef 1111 11110000 abcabcab
  //   contents of rom_2 (hex, n*v repeats v):
  //   40 50 60 70
  //   YOUR REGFILE SHOULD FIT IN HERE!
  //   There should be no blue/red wires here, and the result shouldn't be x's.
endmodule
